# Fritzing sketch arduino_nano-nrf (saved by Fritzing 0.9.3b)
circuit board: 8.46667cm x 5.64444cm
breadboards: 1

parts:
  Part1 = Arduino Nano (Rev3.0)
  Part2 = NRF24L01+ Breakout Board
  S4 = Square Pushbutton
  S5 = Square Pushbutton
  R1 = Resistor [tolerance=±5% resistance=10k package=THT]
  R2 = Resistor [tolerance=±5% resistance=10k package=THT]

nets:
  GND: Part1.GND, Part2.GND, R1.Pin_0, R2.Pin_0
  N1: Part1.D7, S5.leg0, R2.Pin_1
  N2: Part1.D8, S4.leg0, R1.Pin_1
  N3: Part1.D9, Part2.CS
  N4: Part1.D10, Part2.CE
  N5: Part1.D11/MOSI, Part2.MOSI
  N6: Part1.D12/MISO, Part2.MISO
  N7: Part1.5V, S4.leg1, S5.leg1
  3V3: Part1.3V3, Part2.VCC
  N8: Part1.D13/SCK, Part2.SCK
